// Digital circuit ntsc_gen.dig as structural Verilog
module ntsc_gen (
  input  _14_138MHZ
);

  wire _1H, _1V, _2H, _2V, _4H, _4V, _8H, _8V, _16H, _16V, _32H, _32V, _64H, _64V, _128H, _128V, _256H,
       _256V, _512H, _512V, _74060_1_p9, _74060_1_p14, _74060_1_p15, _74060_1_p16, _74060_2_p14,
       _74060_2_p15, _74060_2_p16, and_1_out, and_2_out, and_3_out, and_4_out, and_5_out, and_7_out,
       and_8_out, CLK_7_159MHZ, d_ff_1_nq, HBLANK, HBLANK_t, HRESET, HRESET_t, HSYNC, nand_1_out,
       pulldown_16_out, VBLANK, VBLANK_t, VRESET, VRESET_t, VSYNC;

  LED led_1 (.in(_1V));
  LED led_2 (.in(_2V));
  LED led_3 (.in(_4V));
  LED led_4 (.in(_8V));
  LED led_5 (.in(_16V));
  LED led_6 (.in(_32V));
  LED led_7 (.in(_64V));
  LED led_8 (.in(_128V));
  LED led_9 (.in(_256V));
  LED led_10 (.in(_512V));
  LED led_11 (.in(_2H));
  LED led_12 (.in(_4H));
  LED led_13 (.in(_8H));
  LED led_14 (.in(_16H));
  LED led_15 (.in(_32H));
  LED led_16 (.in(_64H));
  LED led_17 (.in(_128H));
  LED led_18 (.in(_256H));
  LED led_19 (.in(_512H));
  D_FF d_ff_1 (.D(d_ff_1_nq), .C(_14_138MHZ), .Q(CLK_7_159MHZ), .nQ(d_ff_1_nq));
  PullDown pulldown_1 (.out(_1H));
  // Probe 1H on _1H
  PullDown pulldown_2 (.out(_2V));
  PullDown pulldown_3 (.out(_4V));
  PullDown pulldown_4 (.out(_8V));
  PullDown pulldown_5 (.out(_16V));
  PullDown pulldown_6 (.out(_32V));
  PullDown pulldown_7 (.out(_64V));
  PullDown pulldown_8 (.out(_128V));
  PullDown pulldown_9 (.out(_2H));
  PullDown pulldown_10 (.out(_4H));
  PullDown pulldown_11 (.out(_8H));
  PullDown pulldown_12 (.out(_16H));
  PullDown pulldown_13 (.out(_32H));
  PullDown pulldown_14 (.out(_64H));
  PullDown pulldown_15 (.out(_128H));
  PullDown pulldown_16 (.out(pulldown_16_out));
  // ScopeTrigger #(.maxStepCount(2500)) scopetrigger_1: pin names not known; wires that end beside it: _128H
  // _74060 _74060_1: pin names not known; wires that end beside it: _2V, _4V, _8V, _16V, _32V, _64V, _128V, 1'b0, _74060_1_p9, _512V, _256V, 1'b1, _1V, _74060_1_p14, _74060_1_p15, _74060_1_p16, HRESET, VRESET
  PullDown pulldown_17 (.out(_74060_1_p9));
  // _74060 _74060_2: pin names not known; wires that end beside it: _2H, _4H, _8H, _16H, _32H, _64H, _128H, 1'b0, pulldown_16_out, _512H, _256H, 1'b1, _1H, _74060_2_p14, _74060_2_p15, _74060_2_p16, CLK_7_159MHZ, HRESET_t
  PullDown pulldown_18 (.out(_512V));
  PullDown pulldown_19 (.out(_1V));
  PullDown pulldown_20 (.out(_74060_1_p14));
  PullDown pulldown_21 (.out(_74060_1_p15));
  PullDown pulldown_22 (.out(_74060_1_p16));
  PullDown pulldown_23 (.out(_512H));
  PullDown pulldown_24 (.out(_1H));
  PullDown pulldown_25 (.out(_74060_2_p14));
  PullDown pulldown_26 (.out(_74060_2_p15));
  PullDown pulldown_27 (.out(_74060_2_p16));
  PullDown pulldown_28 (.out(_256H));
  PullDown pulldown_29 (.out(_256V));
  // Probe 2H on _2H
  // Probe 4H on _4H
  // Probe 8H on _8H
  // Probe 16H on _16H
  // Probe 32H on _32H
  // Probe 64H on _64H
  // Probe 128H on _128H
  // Probe 256H on _256H
  // Probe 512H on _512H
  // Probe 1V on _1V
  // Probe 2V on _2V
  // Probe 4V on _4V
  // Probe 8V on _8V
  // Probe 16V on _16V
  // Probe 32V on _32V
  // Probe 64V on _64V
  // Probe 128V on _128V
  // Probe 256V on _256V
  // Probe 512V on _512V
  and and_1 (and_1_out, _2H, _4H);
  and and_2 (and_2_out, _64H, _128H);
  nand nand_1 (nand_1_out, _16H, _64H);
  nor nor_1 (VBLANK_t, VRESET_t, VBLANK);
  nor nor_2 (VBLANK, VBLANK_t, _16V);
  and and_3 (and_3_out, and_2_out, _256H);
  nand nand_2 (HBLANK_t, nand_1_out, HBLANK);
  nand nand_3 (HBLANK, HBLANK_t, HRESET_t);
  and and_4 (and_4_out, VBLANK, _8V);
  and and_5 (and_5_out, and_1_out, and_3_out);
  and and_6 (VSYNC, and_4_out, _4V);
  and and_7 (and_7_out, _1V, _4V);
  nand nand_4 (HSYNC, HBLANK, _32H);
  D_FF d_ff_2 (.D(and_5_out), .C(CLK_7_159MHZ), .Q(HRESET), .nQ(HRESET_t));
  and and_8 (and_8_out, and_7_out, _256V);
  LED led_20 (.in(HBLANK));
  LED led_21 (.in(HSYNC));
  LED led_22 (.in(VBLANK_t));
  LED led_23 (.in(VRESET_t));
  D_FF d_ff_3 (.D(and_8_out), .C(HRESET_t), .Q(VRESET_t), .nQ(VRESET));
  LED led_24 (.in(HRESET));
  // Probe hsync- on HSYNC
  // Probe VBLANK- on VBLANK_t
  // Probe VRESET- on VRESET_t
  // Probe hreset on HRESET
  // Probe hblank on HBLANK

  // Notes on the sheet:
  //   _14_138MHZ: Hz: 300
  //   Vertical Timer
  //   Horizontal Timer
  //   Clock Gen
  //   HRESET
  //   VRESET&VSYNC
endmodule
