// Digital circuit 74060.dig as structural Verilog
module _74060 (
  input  nOE,
  input  RCLK,
  input  nCCKEN,
  input  CCLK,
  input  nCCLR,
  input  VCC,
  input  GND,
  output QA,
  output QB,
  output QC,
  output QD,
  output QE,
  output QF,
  output QG,
  output QH,
  output GI,
  output QJ,
  output nRCO
);

  wire and_1_out, and_2_out, and_3_out, and_4_out, and_5_out, and_6_out, and_7_out, and_8_out, and_9_out,
       and_10_out, and_11_out, and_12_out, and_13_out, and_14_out, and_15_out, and_16_out, and_17_out,
       d_ff_1_q, d_ff_2_q, d_ff_3_q, d_ff_4_q, d_ff_5_q, d_ff_6_q, d_ff_7_q, d_ff_8_q, d_ff_9_q, d_ff_10_q,
       jk_ff_as_1_q, jk_ff_as_2_q, jk_ff_as_3_q, jk_ff_as_4_q, jk_ff_as_5_q, jk_ff_as_6_q, jk_ff_as_7_q,
       jk_ff_as_8_q, jk_ff_as_9_q, jk_ff_as_10_q, not_1_out, not_2_out;

  PowerSupply powersupply_1 (.VDD(VCC), .GND(GND));
  not not_1 (not_1_out, nCCKEN);
  not not_2 (not_2_out, nCCLR);
  and and_1 (and_1_out, jk_ff_as_1_q, not_1_out);
  and and_2 (and_2_out, jk_ff_as_2_q, jk_ff_as_1_q);
  and and_3 (and_3_out, and_2_out, not_1_out);
  and and_4 (and_4_out, jk_ff_as_3_q, and_2_out);
  and and_5 (and_5_out, and_4_out, not_1_out);
  and and_6 (and_6_out, jk_ff_as_4_q, and_4_out);
  and and_7 (and_7_out, and_6_out, not_1_out);
  and and_8 (and_8_out, jk_ff_as_5_q, and_6_out);
  and and_9 (and_9_out, and_8_out, not_1_out);
  and and_10 (and_10_out, jk_ff_as_6_q, and_8_out);
  and and_11 (and_11_out, and_10_out, not_1_out);
  and and_12 (and_12_out, jk_ff_as_7_q, and_10_out);
  and and_13 (and_13_out, and_12_out, not_1_out);
  and and_14 (and_14_out, jk_ff_as_8_q, and_12_out);
  and and_15 (and_15_out, and_14_out, not_1_out);
  and and_16 (and_16_out, jk_ff_as_9_q, and_14_out);
  and and_17 (and_17_out, and_16_out, not_1_out);
  JK_FF_AS jk_ff_as_1 (
    .Set(1'b0), .J(not_1_out), .C(CCLK), .K(not_1_out), .Clr(not_2_out), .Q(jk_ff_as_1_q));  // open: nQ
  JK_FF_AS jk_ff_as_2 (
    .Set(1'b0), .J(and_1_out), .C(CCLK), .K(and_1_out), .Clr(not_2_out), .Q(jk_ff_as_2_q));  // open: nQ
  JK_FF_AS jk_ff_as_3 (
    .Set(1'b0), .J(and_3_out), .C(CCLK), .K(and_3_out), .Clr(not_2_out), .Q(jk_ff_as_3_q));  // open: nQ
  JK_FF_AS jk_ff_as_4 (
    .Set(1'b0), .J(and_5_out), .C(CCLK), .K(and_5_out), .Clr(not_2_out), .Q(jk_ff_as_4_q));  // open: nQ
  JK_FF_AS jk_ff_as_5 (
    .Set(1'b0), .J(and_7_out), .C(CCLK), .K(and_7_out), .Clr(not_2_out), .Q(jk_ff_as_5_q));  // open: nQ
  JK_FF_AS jk_ff_as_6 (
    .Set(1'b0), .J(and_9_out), .C(CCLK), .K(and_9_out), .Clr(not_2_out), .Q(jk_ff_as_6_q));  // open: nQ
  JK_FF_AS jk_ff_as_7 (
    .Set(1'b0), .J(and_11_out), .C(CCLK), .K(and_11_out), .Clr(not_2_out), .Q(jk_ff_as_7_q));  // open: nQ
  JK_FF_AS jk_ff_as_8 (
    .Set(1'b0), .J(and_13_out), .C(CCLK), .K(and_13_out), .Clr(not_2_out), .Q(jk_ff_as_8_q));  // open: nQ
  JK_FF_AS jk_ff_as_9 (
    .Set(1'b0), .J(and_15_out), .C(CCLK), .K(and_15_out), .Clr(not_2_out), .Q(jk_ff_as_9_q));  // open: nQ
  JK_FF_AS jk_ff_as_10 (
    .Set(1'b0), .J(and_17_out), .C(CCLK), .K(and_17_out), .Clr(not_2_out), .Q(jk_ff_as_10_q));  // open: nQ
  D_FF d_ff_1 (.D(jk_ff_as_1_q), .C(RCLK), .Q(d_ff_1_q));  // open: nQ
  D_FF d_ff_2 (.D(jk_ff_as_2_q), .C(RCLK), .Q(d_ff_2_q));  // open: nQ
  D_FF d_ff_3 (.D(jk_ff_as_3_q), .C(RCLK), .Q(d_ff_3_q));  // open: nQ
  D_FF d_ff_4 (.D(jk_ff_as_4_q), .C(RCLK), .Q(d_ff_4_q));  // open: nQ
  D_FF d_ff_5 (.D(jk_ff_as_5_q), .C(RCLK), .Q(d_ff_5_q));  // open: nQ
  D_FF d_ff_6 (.D(jk_ff_as_6_q), .C(RCLK), .Q(d_ff_6_q));  // open: nQ
  D_FF d_ff_7 (.D(jk_ff_as_7_q), .C(RCLK), .Q(d_ff_7_q));  // open: nQ
  D_FF d_ff_8 (.D(jk_ff_as_8_q), .C(RCLK), .Q(d_ff_8_q));  // open: nQ
  D_FF d_ff_9 (.D(jk_ff_as_9_q), .C(RCLK), .Q(d_ff_9_q));  // open: nQ
  D_FF d_ff_10 (.D(jk_ff_as_10_q), .C(RCLK), .Q(d_ff_10_q));  // open: nQ
  nand nand_1 (nRCO, jk_ff_as_10_q, and_16_out);
  assign QA = ~nOE ? d_ff_1_q : 1'bz;  // DriverInvSel driverinvsel_1
  assign QB = ~nOE ? d_ff_2_q : 1'bz;  // DriverInvSel driverinvsel_2
  assign QC = ~nOE ? d_ff_3_q : 1'bz;  // DriverInvSel driverinvsel_3
  assign QD = ~nOE ? d_ff_4_q : 1'bz;  // DriverInvSel driverinvsel_4
  assign QE = ~nOE ? d_ff_5_q : 1'bz;  // DriverInvSel driverinvsel_5
  assign QF = ~nOE ? d_ff_6_q : 1'bz;  // DriverInvSel driverinvsel_6
  assign QG = ~nOE ? d_ff_7_q : 1'bz;  // DriverInvSel driverinvsel_7
  assign QH = ~nOE ? d_ff_8_q : 1'bz;  // DriverInvSel driverinvsel_8
  assign GI = ~nOE ? d_ff_9_q : 1'bz;  // DriverInvSel driverinvsel_9
  assign QJ = ~nOE ? d_ff_10_q : 1'bz;  // DriverInvSel driverinvsel_10

  // Notes on the sheet:
  //   nOE: pin 14
  //   RCLK: pin 13
  //   nCCKEN: pin 12
  //   CCLK: pin 11, Hz: 5
  //   nCCLR: pin 10
  //   QA: pin 15
  //   QB: pin 1
  //   QC: pin 2
  //   QD: pin 3
  //   QE: pin 4
  //   QF: pin 5
  //   QG: pin 6
  //   QH: pin 7
  //   VCC: pin 16, default 1
  //   GND: pin 8
  //   GI: pin 6
  //   QJ: pin 7
  //   nRCO: pin 9
endmodule
